# Fritzing sketch Sensoreye Sketch (saved by Fritzing 0.9.0b)

parts:
  Componente1 = Arduino Uno (Rev3) - ICSP
  Componente2 = SRF05 Ultrasonic Rangefinder
  VCC1 = Battery block 9V
  U1 = Vibration Motor- ROB-08449 [package=vibe-motor-10mm]
  S1 = Toggle Switch [package=THT]

nets:
  GND: Componente1.GND, Componente2.GND, U1.+
  N1: Componente1.D12/MISO, Componente2.Echo
  N2: Componente1.D5_PWM, U1.-
  N3: Componente1.D7, Componente2.Trig
  5V: Componente1.5V, Componente2.VCC
  N4: VCC1.+, S1.COM
